// Logisim project design_project_two.circ as structural Verilog: 3 circuits, main circuit half_adder
module half_adder (
  input  in_1,
  input  in_2,
  output sum,
  output carry_in
);

  and and_1 (carry_in, in_1, in_2);
  xor xor_1 (sum, in_1, in_2);
endmodule

module four_bit_adder (
  input  in_1,
  input  in_2,
  input  in_3,
  input  in_4,
  input  in_5,
  input  in_6,
  input  in_7,
  input  in_8,
  output sum_one,
  output carry_in_one,
  output sum_two,
  output carry_in_two,
  output sum_three,
  output carry_in_three,
  output sum_four,
  output carry_in_four
);

  wire half_adder_1_carry_in, half_adder_1_sum, half_adder_2_carry_in, half_adder_2_sum,
       half_adder_3_carry_in, half_adder_3_sum, half_adder_4_carry_in, half_adder_4_sum;

  half_adder half_adder_1 (.in_1(in_1), .in_2(in_2), .sum(half_adder_1_sum), .carry_in(half_adder_1_carry_in));
  half_adder half_adder_2 (.in_1(in_3), .in_2(in_4), .sum(half_adder_2_sum), .carry_in(half_adder_2_carry_in));
  half_adder half_adder_3 (.in_1(in_5), .in_2(in_6), .sum(half_adder_3_sum), .carry_in(half_adder_3_carry_in));
  half_adder half_adder_4 (.in_1(in_7), .in_2(in_8), .sum(half_adder_4_sum), .carry_in(half_adder_4_carry_in));
  half_adder half_adder_5 (.in_1(half_adder_1_sum), .in_2(half_adder_2_sum), .sum(sum_one), .carry_in(carry_in_one));
  half_adder half_adder_6 (
    .in_1(half_adder_1_carry_in), .in_2(half_adder_2_carry_in), .sum(sum_two), .carry_in(carry_in_two));
  half_adder half_adder_7 (
    .in_1(half_adder_3_sum), .in_2(half_adder_4_sum), .sum(sum_three), .carry_in(carry_in_three));
  half_adder half_adder_8 (
    .in_1(half_adder_3_carry_in), .in_2(half_adder_4_carry_in), .sum(sum_four), .carry_in(carry_in_four));
endmodule

module eight_bit_adder (
);

  wire and_1_out, and_2_out, clock_1_out, clock_2_out, clock_3_out, clock_4_out, clock_5_out, clock_6_out,
       clock_7_out, clock_8_out, clock_9_out, four_bit_adder_1_carry_in_four, four_bit_adder_1_carry_in_one,
       four_bit_adder_1_carry_in_three, four_bit_adder_1_carry_in_two, four_bit_adder_1_sum_four,
       four_bit_adder_1_sum_one, four_bit_adder_1_sum_three, four_bit_adder_1_sum_two, half_adder_1_carry_in,
       half_adder_1_sum, half_adder_2_carry_in, half_adder_2_sum, half_adder_3_sum, half_adder_4_carry_in,
       half_adder_4_sum, j_k_ff_1_q, not_1_out, not_2_out, or_1_out, or_2_out, or_3_out, or_4_out, or_5_out;

  Clock #(.highDuration(256), .lowDuration(256)) clock_1 (.out(clock_1_out));
  Clock #(.highDuration(128), .lowDuration(128)) clock_2 (.out(clock_2_out));
  Clock #(.highDuration(64), .lowDuration(64)) clock_3 (.out(clock_3_out));
  Clock #(.highDuration(32), .lowDuration(32)) clock_4 (.out(clock_4_out));
  Clock #(.highDuration(16), .lowDuration(16)) clock_5 (.out(clock_5_out));
  Clock #(.highDuration(8), .lowDuration(8)) clock_6 (.out(clock_6_out));
  Clock #(.highDuration(4), .lowDuration(4)) clock_7 (.out(clock_7_out));
  Clock #(.highDuration(2), .lowDuration(2)) clock_8 (.out(clock_8_out));
  four_bit_adder four_bit_adder_1 (
    .in_1(clock_1_out), .in_2(clock_2_out), .in_3(clock_3_out), .in_4(clock_4_out), .in_5(clock_5_out),
    .in_6(clock_6_out), .in_7(clock_7_out), .in_8(clock_8_out), .sum_one(four_bit_adder_1_sum_one),
    .carry_in_one(four_bit_adder_1_carry_in_one), .sum_two(four_bit_adder_1_sum_two),
    .carry_in_two(four_bit_adder_1_carry_in_two), .sum_three(four_bit_adder_1_sum_three),
    .carry_in_three(four_bit_adder_1_carry_in_three), .sum_four(four_bit_adder_1_sum_four),
    .carry_in_four(four_bit_adder_1_carry_in_four));
  or or_1 (or_1_out, four_bit_adder_1_carry_in_three, four_bit_adder_1_sum_four);
  or or_2 (or_2_out, four_bit_adder_1_carry_in_one, four_bit_adder_1_sum_two);
  half_adder half_adder_1 (
    .in_1(four_bit_adder_1_sum_one), .in_2(four_bit_adder_1_sum_three), .sum(half_adder_1_sum),
    .carry_in(half_adder_1_carry_in));
  half_adder half_adder_2 (.in_1(or_2_out), .in_2(or_1_out), .sum(half_adder_2_sum), .carry_in(half_adder_2_carry_in));
  half_adder half_adder_3 (
    .in_1(four_bit_adder_1_carry_in_two), .in_2(four_bit_adder_1_carry_in_four), .sum(half_adder_3_sum));  // open: carry_in
  or or_3 (or_3_out, half_adder_2_carry_in, half_adder_3_sum);
  half_adder half_adder_4 (
    .in_1(half_adder_1_carry_in), .in_2(half_adder_2_sum), .sum(half_adder_4_sum),
    .carry_in(half_adder_4_carry_in));
  or or_4 (or_4_out, half_adder_4_carry_in, or_3_out);
  LED C (.in(half_adder_1_sum));
  LED B (.in(half_adder_4_sum));
  not not_1 (not_1_out, or_4_out);
  LED A (.in(or_4_out));
  not not_2 (not_2_out, half_adder_4_sum);
  and and_1 (and_1_out, half_adder_4_sum, not_1_out);
  and and_2 (and_2_out, half_adder_1_sum, and_1_out);
  Clock clock_9 (.out(clock_9_out));
  or or_5 (or_5_out, not_2_out, or_4_out);
  J_K_Flip_Flop j_k_ff_1 (.J(and_2_out), .K(or_5_out), .clk(clock_9_out), .Q(j_k_ff_1_q));  // open: Qn, preset, reset
  LED Alive (.in(j_k_ff_1_q));
endmodule
